# Fritzing sketch 4x7segmentTimer (saved by Fritzing 0.9.6b)
breadboards: 1

parts:
  U1 = 7-Segment-Display-4-Red [part_number=HS420561K package="7-Segment-4 [THT]"]
  Part1 = Arduino Uno (Rev3)
  R5 = Resistor [tolerance=±5% resistance=1k package="0402 [SMD]"]
  R6 = Resistor [tolerance=±5% resistance=1k package="0402 [SMD]"]
  R7 = Resistor [tolerance=±5% resistance=1k package="0402 [SMD]"]
  R8 = Resistor [tolerance=±5% resistance=1k package="0402 [SMD]"]

nets:
  N1: U1.pin1, Part1.D1/TX
  N2: U1.pin2, Part1.D2
  N3: U1.pin3, Part1.D3_PWM
  N4: U1.pin4, Part1.D4
  N5: U1.pin5, Part1.D5_PWM
  N6: U1.pin6, R5.Pin_0
  N7: U1.pin7, Part1.D7
  N8: U1.pin8, R6.Pin_0
  N9: U1.pin_9, R7.Pin_0
  N10: U1.pin_10, Part1.D10_PWM/SS
  N11: U1.pin_11, Part1.D11_PWM/MOSI
  N12: U1.pin_12, R8.Pin_0
  N13: Part1.D8, R6.Pin_1
  N14: Part1.D9_PWM, R7.Pin_1
  N15: Part1.D12/MISO, R8.Pin_1
  N16: Part1.D6_PWM, R5.Pin_1

custom parts:
  7-Segment-Display-4-Red: 7-Segment Display 4 digits Red
